// Digital circuit 2-bit-multiplier-circuit.dig as structural Verilog
module _2_bit_multiplier_circuit (
  input  A_1,
  input  A_0,
  input  B_1,
  input  B_0,
  output P_0,
  output P_1,
  output P_3,
  output P_2
);

  wire and_1_out, and_2_out, and_3_out, and_5_out;

  and and_1 (and_1_out, B_1, A_1);
  and and_2 (and_2_out, B_1, A_0);
  and and_3 (and_3_out, B_0, A_1);
  and and_4 (P_0, B_0, A_0);
  and and_5 (and_5_out, and_2_out, and_3_out);
  xor xor_1 (P_1, and_2_out, and_3_out);
  and and_6 (P_3, and_1_out, and_5_out);
  xor xor_2 (P_2, and_1_out, and_5_out);
endmodule
