// Digital circuit 4-bit-full-adder.dig as structural Verilog
module _4_bit_full_adder (
  input  [3:0] A,
  input  [3:0] B,
  output [3:0] Sum,
  output Overflow_flag
);

  wire _1_bit_adder_1_p3, _1_bit_adder_2_p3, _1_bit_adder_3_p3;
  wire [3:0] _1_bit_adder_1_p1, _1_bit_adder_1_p2, _1_bit_adder_1_p4, _1_bit_adder_2_p1, _1_bit_adder_2_p2,
       _1_bit_adder_2_p4, _1_bit_adder_3_p1, _1_bit_adder_3_p2, _1_bit_adder_3_p4;

  // _1_bit_adder _1_bit_adder_1: pin names not known; wires that end beside it: _1_bit_adder_1_p1, _1_bit_adder_1_p2, _1_bit_adder_1_p3, _1_bit_adder_1_p4, Overflow_flag
  // _1_bit_adder _1_bit_adder_2: pin names not known; wires that end beside it: _1_bit_adder_2_p1, _1_bit_adder_2_p2, _1_bit_adder_2_p3, _1_bit_adder_2_p4, _1_bit_adder_1_p3
  // _1_bit_adder _1_bit_adder_3: pin names not known; wires that end beside it: _1_bit_adder_3_p1, _1_bit_adder_3_p2, _1_bit_adder_3_p3, _1_bit_adder_3_p4, _1_bit_adder_2_p3
  // _1_bit_adder _1_bit_adder_4: pin names not known; wires that end beside it: B, A, 1'b0, Sum, _1_bit_adder_3_p3
  // Pins of 1 and 4 bits meet at A
  // Pins of 1 and 4 bits meet at B
  // Pins of 1 and 4 bits meet at Sum
endmodule
